# Fritzing sketch capstoneV2 (saved by Fritzing 0.9.9b)

parts:
  Main_Control_Unit = Raspberry Pi 4B
  LCD_Display = LCD1602-I2C
  Camera = Rasberry Pi NIOR Camera [chip_label=IC package="DIP (Dual Inline) [THT]"]  # not connected
  HC-SR04_Sensor_1 = HC-SR04 Ultrasonic Distance Sensor
  R1 = Resistor [tolerance=±20% power=0.25 resistance=1000 package=THT]
  R2 = Resistor [tolerance=±20% power=0.25W resistance=1000 package=THT]
  R3 = Resistor [tolerance=±20% power=0.25 resistance=1000 package=THT]

nets:
  VCC: Main_Control_Unit.5V, LCD_Display.VCC, HC-SR04_Sensor_1.VCC
  N1: Main_Control_Unit.GPIO2, LCD_Display.SDA
  N2: Main_Control_Unit.GPIO3, LCD_Display.SCL
  GND: Main_Control_Unit.GND, LCD_Display.GND, HC-SR04_Sensor_1.GND, R3.Pin_0
  N3: Main_Control_Unit.GPIO23, HC-SR04_Sensor_1.TRIG
  N4: Main_Control_Unit.GPIO24, R1.Pin_1, R2.Pin_0
  N5: HC-SR04_Sensor_1.ECHO, R1.Pin_0
  N6: R2.Pin_1, R3.Pin_1

notes:
  Camera will be connected to the camera port available on the motherboard

custom parts:
  LCD1602-I2C: A standard character display, usually with 2x16 characters. Comes in many colors with LCM1602 IIC attached.
  Rasberry Pi NIOR Camera: Camera
